# Fritzing sketch SimonSketch (saved by Fritzing 0.9.2b)
breadboards: 1

parts:
  LED1 = LED - 5mm [color="Yellow (595nm)" package="5 mm [THT]"]
  LED2 = LED - 5mm [color="Green (570nm)" package="5 mm [THT]"]
  LED3 = LED - 5mm [color="Red (633nm)" package="5 mm [THT]"]
  LED4 = LED - 5mm [color="Blue (525nm)" package="5 mm [THT]"]
  S1 = Pushbutton [package="[THT]"]
  S2 = Pushbutton [package="[THT]"]
  S3 = Pushbutton [package="[THT]"]
  S4 = Pushbutton [package="[THT]"]
  R1 = Resistor [tolerance=±5% resistance=220 package=THT]
  R2 = Resistor [tolerance=±5% resistance=220 package=THT]
  R3 = Resistor [tolerance=±5% resistance=220 package=THT]
  R4 = Resistor [tolerance=±5% resistance=220 package=THT]
  R5 = Resistor [tolerance=±5% resistance=10k package=THT]
  R6 = Resistor [tolerance=±5% resistance=10k package=THT]
  R7 = Resistor [tolerance=±5% resistance=10k package=THT]
  R8 = Resistor [tolerance=±5% resistance=10k package=THT]
  Part1 = Arduino Uno (Rev3)

nets:
  N1: LED1.cathode, R1.Pin_1
  N2: LED1.anode, Part1.D2
  N3: LED2.cathode, R2.Pin_1
  N4: LED2.anode, Part1.D3_PWM
  N5: LED3.cathode, R3.Pin_1
  N6: LED3.anode, Part1.D4
  N7: LED4.cathode, R4.Pin_1
  N8: LED4.anode, Part1.D5_PWM
  N9: S1.Pin_1, S1.Pin_2, R5.Pin_0, Part1.D6_PWM
  N10: S1.Pin_3, S1.Pin_4, S2.Pin_3, S2.Pin_4, S3.Pin_3, S3.Pin_4, S4.Pin_3, S4.Pin_4, Part1.5V
  N11: S2.Pin_1, S2.Pin_2, R6.Pin_0, Part1.D7
  N12: S3.Pin_1, S3.Pin_2, R7.Pin_0, Part1.D8
  N13: S4.Pin_1, S4.Pin_2, R8.Pin_0, Part1.D9_PWM
  N14: R1.Pin_0, R2.Pin_0, R3.Pin_0, R4.Pin_0, R5.Pin_1, R6.Pin_1, R7.Pin_1, R8.Pin_1, Part1.GND
